# Fritzing sketch PoolTechClimateControl-DT-J2H3DK3 (saved by Fritzing 0.9.10b)
breadboards: 2

parts:
  HLK-PM1 = HLK-PM01
  Part1 = Arduino Nano (Rev3.0) (ICSP)
  DHT1 = DHT22 Humidity and Temperature Sensor
  DHT2 = DHT22 Humidity and Temperature Sensor
  DHT3 = DHT22 Humidity and Temperature Sensor
  DHT4 = DHT22 Humidity and Temperature Sensor
  Part2 = Tiny RTC - DS1307 Breakout Board
  R1 = Resistor [tolerance=±5% power=0.25 resistance=10k package=THT]
  R2 = Resistor [tolerance=±5% power=0.25 resistance=10k package=THT]
  R3 = Resistor [tolerance=±5% power=0.25 resistance=10k package=THT]
  R4 = Resistor [tolerance=±5% power=0.25 resistance=10k package=THT]
  LED1 = smd LED [color="Red (633nm)" package="0603 [SMD]"]
  LED2 = smd LED [color="Green (570nm)" package="0603 [SMD]"]
  R5 = Resistor [tolerance=±5% power=0.25 resistance=570 package=THT]
  R6 = Resistor [tolerance=±5% power=0.25 resistance=570 package=THT]
  S1 = Pushbutton [package="[THT]"]

nets:
  GND: HLK-PM1.-Vo, Part1.GND, DHT1.GND, DHT2.GND, DHT3.GND, DHT4.GND, Part2.GND, R5.Pin_0, R6.Pin_0, S1.Pin_3, S1.Pin_4
  VDD: HLK-PM1.+Vo, Part1.5V, DHT1.VDD, DHT2.VDD, DHT3.VDD, DHT4.VDD, Part2.VCC, R1.Pin_0, R2.Pin_0, R3.Pin_0, R4.Pin_0, LED2.anode
  N1: Part1.D3, S1.Pin_1, S1.Pin_2
  N2: Part1.D4, DHT4.DATA, R4.Pin_1
  N3: Part1.D5, DHT3.DATA, R3.Pin_1
  N4: Part1.D7, DHT2.DATA, R2.Pin_1
  N5: Part1.D8, DHT1.DATA, R1.Pin_1
  N6: Part1.D9, LED1.anode
  N7: Part1.A5, Part2.SCL
  N8: Part1.A4, Part2.SDA
  N9: LED1.cathode, R5.Pin_1
  N10: LED2.cathode, R6.Pin_1

custom parts:
  Tiny RTC - DS1307 Breakout Board: The Tiny RTC is a breakout board for the Dallas Semiconductor/Maxim Integrated DS1307 real-time clock. The DS1307 counts seconds, minutes, hours, date of the month, month, day of the week, and year (with compensation for leap-years). The breakout board also has space for a DS18B20 digital thermometer.
